# Fritzing sketch ps2toatarijoy (saved by Fritzing 0.9.3b)

parts:
  Εξάρτημα1 = Arduino Uno (Rev3)
  X1 = DB9 Connector [package=db9]
  JP1 = Header 10 [package=1x10-2mm-smd]

nets:
  N1: Εξάρτημα1.D10_PWM/SS, JP1.7
  N2: Εξάρτημα1.D11_PWM/MOSI, JP1.6
  N3: Εξάρτημα1.D12/MISO, JP1.2
  N4: Εξάρτημα1.D13/SCK, JP1.1
  N5: Εξάρτημα1.D2, X1.1
  N6: Εξάρτημα1.D4, X1.6
  N7: Εξάρτημα1.D5_PWM, X1.7
  N8: Εξάρτημα1.D6_PWM, X1.8
  N9: Εξάρτημα1.D7, X1.9
  N10: Εξάρτημα1.3V3, JP1.5
  N11: Εξάρτημα1.GND, JP1.4
